// Logisim project Lab1.circ as structural Verilog
module CXOR (
  input  A,
  input  B,
  output S
);

  wire and_1_out, and_2_out, not_1_out, not_2_out;

  not not_1 (not_1_out, A);
  not not_2 (not_2_out, B);
  and and_1 (and_1_out, A, not_2_out);
  and and_2 (and_2_out, not_1_out, B);
  or or_1 (S, and_1_out, and_2_out);

  // Notes on the sheet:
  //   CIRCUITO XOR
endmodule

module MUX2 (
  input  A,
  input  B,
  input  C,
  output S
);

  wire and_1_out, and_2_out, not_1_out;

  not not_1 (not_1_out, C);
  and and_1 (and_1_out, A, not_1_out);
  and and_2 (and_2_out, B, C);
  or or_1 (S, and_1_out, and_2_out);

  // Notes on the sheet:
  //   CIRCUITO MUX2
endmodule

module MUX4 (
  input  C0,
  input  C1,
  input  A,
  input  B,
  input  C,
  input  D,
  output S
);

  wire and_1_out, and_2_out, and_3_out, and_4_out, not_1_out, not_2_out;

  not not_1 (not_1_out, C0);
  not not_2 (not_2_out, C1);
  and and_1 (and_1_out, A, not_1_out, not_2_out);
  and and_2 (and_2_out, B, not_1_out, C1);
  and and_3 (and_3_out, C, C0, not_2_out);
  and and_4 (and_4_out, D, C0, C1);
  or or_1 (S, and_1_out, and_2_out, and_3_out, and_4_out);

  // Notes on the sheet:
  //   CIRCUITO MUX4
endmodule

module ADD1 (
  input  A,
  input  B,
  input  Cin,
  output S,
  output Cout
);

  wire and_1_out, and_2_out, cxor_1_s;

  and and_1 (and_1_out, A, B);
  and and_2 (and_2_out, cxor_1_s, Cin);
  CXOR cxor_1 (.A(A), .B(B), .S(cxor_1_s));
  or or_1 (Cout, and_1_out, and_2_out);
  CXOR cxor_2 (.A(cxor_1_s), .B(Cin), .S(S));

  // Notes on the sheet:
  //   CIRCUITO ADD1
endmodule

module ADD8 (
  input  Cin,
  input  [7:0] A,
  input  [7:0] B,
  output [7:0] S,
  output Cout
);

  wire add1_1_cout, add1_2_cout, add1_3_cout, add1_4_cout, add1_5_cout, add1_6_cout, add1_7_cout;

  ADD1 add1_1 (.A(A[0]), .B(B[0]), .Cin(Cin), .S(S[0]), .Cout(add1_1_cout));
  ADD1 add1_2 (.A(A[1]), .B(B[1]), .Cin(add1_1_cout), .S(S[1]), .Cout(add1_2_cout));
  ADD1 add1_3 (.A(A[2]), .B(B[2]), .Cin(add1_2_cout), .S(S[2]), .Cout(add1_3_cout));
  ADD1 add1_4 (.A(A[3]), .B(B[3]), .Cin(add1_3_cout), .S(S[3]), .Cout(add1_4_cout));
  ADD1 add1_5 (.A(A[4]), .B(B[4]), .Cin(add1_4_cout), .S(S[4]), .Cout(add1_5_cout));
  ADD1 add1_6 (.A(A[5]), .B(B[5]), .Cin(add1_5_cout), .S(S[5]), .Cout(add1_6_cout));
  ADD1 add1_7 (.A(A[6]), .B(B[6]), .Cin(add1_6_cout), .S(S[6]), .Cout(add1_7_cout));
  ADD1 add1_8 (.A(A[7]), .B(B[7]), .Cin(add1_7_cout), .S(S[7]), .Cout(Cout));

  // Notes on the sheet:
  //   CIRCUITO ADD8
endmodule

module ALU (
  input  [1:0] OP,
  input  [7:0] B,
  input  [7:0] A,
  input  in_4,
  input  in_5,
  output [7:0] R,
  output zero,
  output out_8,
  output out_9
);

  wire [7:0] add8_1_s, add8_2_s, and_1_out, not_1_out, or_1_out;

  assign not_1_out = ~B;  // NOT_Gate not_1, 8 bits wide
  assign and_1_out = A & B;  // AND_Gate and_1, 8 bits wide
  assign or_1_out = A | B;  // OR_Gate or_1, 8 bits wide
  ADD8 add8_1 (.Cin(in_4), .A(A), .B(B), .S(add8_1_s), .Cout(out_8));
  ADD8 add8_2 (.Cin(in_5), .A(A), .B(not_1_out), .S(add8_2_s), .Cout(out_9));
  MUX4de8bits mux4de8bits_1 (.A(and_1_out), .B(or_1_out), .C(add8_1_s), .D(add8_2_s), .C0(OP), .S(R));
  nor nor_1 (zero, R[7], R[6], R[5], R[4], R[3], R[2], R[1], R[0]);

  // Notes on the sheet:
  //   CIRCUITO ALU
endmodule

module MUX4de8bits (
  input  [7:0] A,
  input  [7:0] B,
  input  [7:0] C,
  input  [7:0] D,
  input  [1:0] C0,
  output [7:0] S
);

  wire [7:0] mux2de8bits_1_s, mux2de8bits_2_s;

  MUX2de8bits mux2de8bits_1 (.A(A), .B(B), .C0(C0[0]), .S(mux2de8bits_1_s));
  MUX2de8bits mux2de8bits_2 (.A(C), .B(D), .C0(C0[0]), .S(mux2de8bits_2_s));
  MUX2de8bits mux2de8bits_3 (.A(mux2de8bits_1_s), .B(mux2de8bits_2_s), .C0(C0[1]), .S(S));

  // Notes on the sheet:
  //   CIRCUITO MUX4 CON SALIDA DE 8 BITS
endmodule

module MUX2de8bits (
  input  [7:0] A,
  input  [7:0] B,
  input  C0,
  output [7:0] S
);

  wire not_1_out;
  wire [7:0] and_1_out, and_2_out, bit_extender_1_out, bit_extender_2_out;

  assign bit_extender_1_out = {{7{C0}}, C0};  // Bit_Extender bit_extender_1
  assign bit_extender_2_out = {{7{not_1_out}}, not_1_out};  // Bit_Extender bit_extender_2
  not not_1 (not_1_out, C0);
  assign and_1_out = A & bit_extender_2_out;  // AND_Gate and_1, 8 bits wide
  assign and_2_out = B & bit_extender_1_out;  // AND_Gate and_2, 8 bits wide
  assign S = and_1_out | and_2_out;  // OR_Gate or_1, 8 bits wide

  // Notes on the sheet:
  //   CIRCUITO MUX2 CON SALIDA DE 8 BITS
endmodule
