// Logisim project Lab2.circ as structural Verilog
module CXOR (
  input  A,
  input  B,
  output S
);

  wire and_1_out, and_2_out, not_1_out, not_2_out;

  not not_1 (not_1_out, A);
  not not_2 (not_2_out, B);
  and and_1 (and_1_out, A, not_2_out);
  and and_2 (and_2_out, not_1_out, B);
  or or_1 (S, and_1_out, and_2_out);

  // Notes on the sheet:
  //   CIRCUITO XOR
endmodule

module MUX2 (
  input  A,
  input  B,
  input  S,
  output R
);

  wire and_1_out, and_2_out, not_1_out;

  not not_1 (not_1_out, S);
  and and_1 (and_1_out, A, not_1_out);
  and and_2 (and_2_out, B, S);
  or or_1 (R, and_1_out, and_2_out);

  // Notes on the sheet:
  //   CIRCUITO MUX2
endmodule

module MUX4 (
  input  I0,
  input  I1,
  input  I2,
  input  I3,
  input  [1:0] S,
  output R
);

  wire mux2_1_r, mux2_2_r;

  MUX2 mux2_1 (.A(I0), .B(I1), .S(S[0]), .R(mux2_1_r));
  MUX2 mux2_2 (.A(I2), .B(I3), .S(S[0]), .R(mux2_2_r));
  MUX2 mux2_3 (.A(mux2_1_r), .B(mux2_2_r), .S(S[1]), .R(R));

  // Notes on the sheet:
  //   CIRCUITO MUX4
endmodule

module ADD1 (
  input  A,
  input  B,
  input  Cin,
  output S,
  output Cout
);

  wire and_1_out, and_2_out, cxor_1_s;

  and and_1 (and_1_out, A, B);
  and and_2 (and_2_out, cxor_1_s, Cin);
  CXOR cxor_1 (.A(A), .B(B), .S(cxor_1_s));
  or or_1 (Cout, and_1_out, and_2_out);
  CXOR cxor_2 (.A(cxor_1_s), .B(Cin), .S(S));

  // Notes on the sheet:
  //   CIRCUITO ADD1
endmodule

module ADD8 (
  input  Cin,
  input  [7:0] A,
  input  [7:0] B,
  output [7:0] S,
  output Cout
);

  wire add1_1_cout, add1_2_cout, add1_3_cout, add1_4_cout, add1_5_cout, add1_6_cout, add1_7_cout;

  ADD1 add1_1 (.A(A[0]), .B(B[0]), .Cin(Cin), .S(S[0]), .Cout(add1_1_cout));
  ADD1 add1_2 (.A(A[1]), .B(B[1]), .Cin(add1_1_cout), .S(S[1]), .Cout(add1_2_cout));
  ADD1 add1_3 (.A(A[2]), .B(B[2]), .Cin(add1_2_cout), .S(S[2]), .Cout(add1_3_cout));
  ADD1 add1_4 (.A(A[3]), .B(B[3]), .Cin(add1_3_cout), .S(S[3]), .Cout(add1_4_cout));
  ADD1 add1_5 (.A(A[4]), .B(B[4]), .Cin(add1_4_cout), .S(S[4]), .Cout(add1_5_cout));
  ADD1 add1_6 (.A(A[5]), .B(B[5]), .Cin(add1_5_cout), .S(S[5]), .Cout(add1_6_cout));
  ADD1 add1_7 (.A(A[6]), .B(B[6]), .Cin(add1_6_cout), .S(S[6]), .Cout(add1_7_cout));
  ADD1 add1_8 (.A(A[7]), .B(B[7]), .Cin(add1_7_cout), .S(S[7]), .Cout(Cout));

  // Notes on the sheet:
  //   CIRCUITO ADD8
endmodule

module ALU (
  input  [7:0] A,
  input  [7:0] B,
  input  [1:0] OP,
  input  in_4,
  output [7:0] R,
  output Zero,
  output out_7,
  output out_8
);

  wire [7:0] add8_1_s, add8_2_s, and_1_out, not_1_out, or_1_out;

  assign not_1_out = ~B;  // NOT_Gate not_1, 8 bits wide
  assign and_1_out = A & B;  // AND_Gate and_1, 8 bits wide
  assign or_1_out = A | B;  // OR_Gate or_1, 8 bits wide
  ADD8 add8_1 (.Cin(in_4), .A(A), .B(B), .S(add8_1_s), .Cout(out_7));
  ADD8 add8_2 (.Cin(1'b1), .A(A), .B(not_1_out), .S(add8_2_s), .Cout(out_8));
  MUX4de8bits mux4de8bits_1 (.A(and_1_out), .B(or_1_out), .C(add8_1_s), .D(add8_2_s), .C0(OP), .S(R));
  nor nor_1 (Zero, R[7], R[6], R[5], R[4], R[3], R[2], R[1], R[0]);

  // Notes on the sheet:
  //   CIRCUITO ALU
endmodule

module MUX4de8bits (
  input  [7:0] A,
  input  [7:0] B,
  input  [7:0] C,
  input  [7:0] D,
  input  [1:0] C0,
  output [7:0] S
);

  wire [7:0] mux2de8bits_1_s, mux2de8bits_2_s;

  MUX2de8bits mux2de8bits_1 (.A(A), .B(B), .C0(C0[0]), .S(mux2de8bits_1_s));
  MUX2de8bits mux2de8bits_2 (.A(C), .B(D), .C0(C0[0]), .S(mux2de8bits_2_s));
  MUX2de8bits mux2de8bits_3 (.A(mux2de8bits_1_s), .B(mux2de8bits_2_s), .C0(C0[1]), .S(S));

  // Notes on the sheet:
  //   CIRCUITO MUX4 CON SALIDA DE 8 BITS
endmodule

module MUX2de8bits (
  input  [7:0] A,
  input  [7:0] B,
  input  C0,
  output [7:0] S
);

  wire [7:0] and_1_out, and_2_out;
  wire [7:7] not_1_out;

  not not_1 (not_1_out[7], C0);
  assign and_1_out = A & {8{not_1_out[7]}};  // AND_Gate and_1, 8 bits wide
  assign and_2_out = B & {8{C0}};  // AND_Gate and_2, 8 bits wide
  assign S = and_1_out | and_2_out;  // OR_Gate or_1, 8 bits wide

  // Notes on the sheet:
  //   CIRCUITO MUX2 CON SALIDA DE 8 BITS
endmodule

module RSLatch (
  input  R,
  input  S,
  output Q,
  output Qbar
);

  nor nor_1 (Q, R, Qbar);
  nor nor_2 (Qbar, Q, S);

  // Notes on the sheet:
  //   Circuito RS Latch
endmodule

module CrossCoupedInverterPair (
  output out_1,
  output out_2
);

  not not_1 (out_1, out_2);
  not not_2 (out_2, out_1);
endmodule

module DLatch (
  input  CLK,
  input  D,
  output Q,
  output NQ
);

  wire and_1_out, and_2_out, not_1_out;

  not not_1 (not_1_out, D);
  and and_1 (and_1_out, CLK, not_1_out);
  and and_2 (and_2_out, CLK, D);
  RSLatch rslatch_1 (.R(and_1_out), .S(and_2_out), .Q(Q), .Qbar(NQ));

  // Notes on the sheet:
  //   Circuito Latch D
endmodule

module DFlipFlop (
  input  CLK,
  input  D,
  output Q,
  output NQ
);

  wire dlatch_1_q, not_1_out;

  not not_1 (not_1_out, CLK);
  DLatch dlatch_1 (.CLK(not_1_out), .D(D), .Q(dlatch_1_q));  // open: NQ
  DLatch dlatch_2 (.CLK(CLK), .D(dlatch_1_q), .Q(Q), .NQ(NQ));
endmodule

module FlipFlopEnabled (
  input  CLK,
  input  EN,
  input  D,
  output Q,
  output NQ
);

  wire and_1_out;

  and and_1 (and_1_out, CLK, EN);
  DFlipFlop dflipflop_1 (.CLK(and_1_out), .D(D), .Q(Q), .NQ(NQ));
endmodule

module LatchDLogisim (
  input  D,
  input  CLK,
  output Q,
  output out_4
);

  DFlipFlop dflipflop_1 (.CLK(CLK), .D(D), .Q(Q));  // open: NQ
  DLatch dlatch_1 (.CLK(CLK), .D(D), .Q(out_4));  // open: NQ
endmodule

module DFF_RISE_FALL (
  input  CLK,
  input  D,
  output Q_RISE,
  output Q_FALL
);

  wire not_1_out;

  not not_1 (not_1_out, CLK);
  DFlipFlop DFF_RISE (.CLK(CLK), .D(D), .Q(Q_RISE));  // open: NQ
  DFlipFlop DFF_FALL (.CLK(not_1_out), .D(D), .Q(Q_FALL));  // open: NQ
endmodule

module FF_D_J_JK (
  input  D,
  input  T,
  input  J,
  input  K,
  input  CKL,
  output Q_D,
  output Q_T,
  output Q_JK
);

  D_Flip_Flop FF_D (.D(D), .clk(CKL), .Q(Q_D));  // open: Qn, preset, reset
  T_Flip_Flop FF_T (.T(T), .clk(CKL), .Q(Q_T));  // open: Qn, reset, preset
  J_K_Flip_Flop FF_JK (.J(J), .K(K), .clk(CKL), .Q(Q_JK));  // open: Qn, preset, reset
endmodule
